// Logisim project lab10part2.circ as structural Verilog: 2 circuits, main circuit main
module main (
  input  Clear,
  output A,
  output B
);

  wire clock_1_out, or_1_out;

  Clock clock_1 (.out(clock_1_out));
  or or_1 (or_1_out, A, B);
  J_K_Flip_Flop j_k_ff_1 (
    .J(or_1_out), .clk(clock_1_out), .K(1'b0), .Q(A), .en(1'b1), .reset(Clear));  // open: Qn, preset
  J_K_Flip_Flop j_k_ff_2 (
    .J(1'b1), .clk(clock_1_out), .K(or_1_out), .Q(B), .en(1'b1), .reset(Clear));  // open: Qn, preset
endmodule

module lab10part2 (
  input  Clear,
  input  Preset,
  output A,
  output B
);

  wire and_1_out, clock_1_out, not_1_out;

  Clock clock_1 (.out(clock_1_out));
  and and_1 (and_1_out, A, B);
  not not_1 (not_1_out, and_1_out);
  J_K_Flip_Flop j_k_ff_1 (
    .J(1'b1), .clk(clock_1_out), .K(and_1_out), .Q(A), .preset(Preset), .en(1'b1), .reset(Clear));  // open: Qn
  J_K_Flip_Flop j_k_ff_2 (
    .J(1'b0), .clk(clock_1_out), .K(not_1_out), .Q(B), .preset(Preset), .en(1'b1), .reset(Clear));  // open: Qn
endmodule
